# Fritzing sketch bernardo (saved by Fritzing 0.9.2b)
circuit board: 10cm x 16cm

parts:
  R1 = Rotary Potentiometer (Small) [maximum_resistance=100kΩ package=THT]
  R2 = Rotary Potentiometer (Small) [maximum_resistance=100kΩ package=THT]
  R3 = Rotary Potentiometer (Small) [maximum_resistance=100kΩ package=THT]
  R4 = Rotary Potentiometer (Small) [maximum_resistance=100kΩ package=THT]
  R5 = Rotary Potentiometer (Small) [maximum_resistance=100kΩ package=THT]
  S1 = SWITCH-MOMENTARY-2 [package=tactile-pth-12mm]
  J1 = female pin header, 10 pins [form="♀ (female)"]
  Power_plug1 = Power plug
  J2 = female pin header, 10 pins [form="♀ (female)"]

nets:
  N1: R1.leg1, R2.leg2, R3.leg1, R4.leg1, R5.leg2, J1.pin1, Power_plug1.VCC, J2.pin1, J2.pin4, J2.pin5, J2.pin8, J2.pin9
  N2: R1.wiper, J1.pin3
  N3: R1.leg2, R2.leg1, R3.leg2, R4.leg2, R5.leg1, S1.1, S1.pin_3, J1.pin2, Power_plug1.GND, J2.pin2, J2.pin3, J2.pin6, J2.pin7, J2.pin10
  N4: R2.wiper, J1.pin4
  N5: R3.wiper, J1.pin5
  N6: R4.wiper, J1.pin6
  N7: R5.wiper, J1.pin7
  N8: S1.2, S1.pin_4, J1.pin8

custom parts:
  SWITCH-MOMENTARY-2: Various NO switches- pushbuttons, reed, etc
