# Fritzing sketch igor (saved by Fritzing 0.9.2b)
circuit board: 10cm x 16cm

parts:
  S1 = SWITCH-MOMENTARY-2 [package=tactile-pth-12mm]
  S2 = SWITCH-MOMENTARY-2 [package=tactile-pth-12mm]
  S3 = SWITCH-MOMENTARY-2 [package=tactile-pth-12mm]
  LED1 = LED - 5mm [color="Red (633nm)" package="5 mm [THT]"]
  R1 = Resistor [tolerance=±5% resistance=220 package=THT]
  R2 = Rotary Potentiometer (Small) [maximum_resistance=100kΩ package=THT]
  R3 = Rotary Potentiometer (Small) [maximum_resistance=100kΩ package=THT]
  S4 = SWITCH-MOMENTARY-2 [package=tactile-pth-12mm]
  LED2 = LED - 5mm [color="Red (633nm)" package="5 mm [THT]"]
  R4 = Resistor [tolerance=±5% resistance=220 package=THT]
  R5 = Rotary Potentiometer (Small) [maximum_resistance=100kΩ package=THT]
  R6 = Rotary Potentiometer (Small) [maximum_resistance=100kΩ package=THT]
  S5 = SWITCH-MOMENTARY-2 [package=tactile-pth-12mm]
  LED3 = LED - 5mm [color="Red (633nm)" package="5 mm [THT]"]
  R7 = Resistor [tolerance=±5% resistance=220 package=THT]
  R8 = Rotary Potentiometer (Small) [maximum_resistance=100kΩ package=THT]
  R9 = Rotary Potentiometer (Small) [maximum_resistance=100kΩ package=THT]
  S6 = SWITCH-MOMENTARY-2 [package=tactile-pth-12mm]
  LED4 = LED - 5mm [color="Red (633nm)" package="5 mm [THT]"]
  R10 = Resistor [tolerance=±5% resistance=220 package=THT]
  R11 = Rotary Potentiometer (Small) [maximum_resistance=100kΩ package=THT]
  R12 = Rotary Potentiometer (Small) [maximum_resistance=100kΩ package=THT]
  U1 = 7-SEGMENT-DISPLAY [package=7-segment-display]
  IC1 = SELECTOR_MULTIPLEXER [package=dil16]
  IC2 = SELECTOR_MULTIPLEXER [package=dil16]
  IC3 = SELECTOR_MULTIPLEXER [package=dil16]
  IC4 = SELECTOR_MULTIPLEXER [package=dil16]
  J1 = female pin header, 30 pins [form="♀ (female)"]
  R13 = Resistor [tolerance=±5% resistance=220 package=THT]
  Power_plug1 = Power plug

nets:
  N1: S1.1, S1.pin_3, S2.1, S2.pin_3, S3.1, S3.pin_3, R1.Pin_1, R2.leg2, R3.leg1, S4.1, S4.pin_3, R4.Pin_1, R5.leg2, R6.leg1, S5.1, S5.pin_3, R7.Pin_1, R8.leg1, R9.leg2, S6.1, S6.pin_3, R10.Pin_1, R11.leg1, R12.leg2, IC1.A_2B, IC1.A_2Y, IC1.P_GND, IC2.A_2B, IC2.A_2Y, IC2.P_GND, IC3.A_2B, IC3.A_2Y, IC3.P_GND, IC4.A_2B, IC4.A_2Y, IC4.P_GND, J1.pin5, J1.pin6, R13.Pin_1, Power_plug1.GND
  N2: S1.2, S1.pin_4, IC1.A_4Y
  N3: S2.2, S2.pin_4, IC1.A_4B
  N4: S3.2, S3.pin_4, IC1.A_4A
  N5: LED1.cathode, R1.Pin_0
  N6: LED1.anode, IC3.A_G
  N7: R2.leg1, R3.leg2, R5.leg1, R6.leg2, R8.leg2, R9.leg1, R11.leg2, R12.leg1, IC1.P_VCC, IC2.P_VCC, IC3.P_VCC, IC4.P_VCC, J1.pin7, J1.pin8, Power_plug1.VCC
  N8: R2.wiper, IC2.A_4B
  N9: R3.wiper, IC2.A_4Y
  N10: S4.pin_4, IC1.A_G
  N11: LED2.cathode, R4.Pin_0
  N12: LED2.anode, IC3.A_4A
  N13: R5.wiper, IC2.A_G
  N14: R6.wiper, IC2.A_4A
  N15: S5.pin_4, IC1.A_!A!_B
  N16: LED3.cathode, R7.Pin_0
  N17: LED3.anode, IC3.A_4B
  N18: R8.wiper, IC2.A_!A!_B
  N19: R9.wiper, IC2.A_1A
  N20: S6.pin_4, IC1.A_1A
  N21: LED4.cathode, R10.Pin_0
  N22: LED4.anode, IC3.A_4Y
  N23: R11.wiper, IC2.A_2A
  N24: R12.wiper, IC2.A_1Y
  N25: U1.E, IC4.A_4Y
  N26: U1.D, IC4.A_4B
  N27: U1.G1, R13.Pin_0
  N28: U1.C, IC4.A_4A
  N29: U1.DP, IC4.A_G
  N30: U1.B, IC4.A_2A
  N31: U1.A, IC4.A_1Y
  N32: U1.F, IC4.A_1A
  N33: U1.G, IC4.A_!A!_B
  N34: IC1.A_1B, J1.pin21
  N35: IC1.A_3Y, J1.pin23
  N36: IC1.A_3B, J1.pin24
  N37: IC1.A_3A, J1.pin22
  N38: IC2.A_1B, J1.pin17
  N39: IC2.A_3Y, J1.pin19
  N40: IC2.A_3B, J1.pin20
  N41: IC2.A_3A, J1.pin18
  N42: IC3.A_1B, J1.pin1
  N43: IC3.A_3Y, J1.pin3
  N44: IC3.A_3B, J1.pin2
  N45: IC3.A_3A, J1.pin4
  N46: IC4.A_1B, J1.pin26
  N47: IC4.A_3Y, J1.pin28
  N48: IC4.A_3B, J1.pin29
  N49: IC4.A_3A, J1.pin27

custom parts:
  SWITCH-MOMENTARY-2: Various NO switches- pushbuttons, reed, etc
