# Fritzing sketch mariana_costa (saved by Fritzing 0.9.2b)
circuit board: 16cm x 10cm

parts:
  Power_plug1 = Power plug
  J1 = female pin header, 20 pins [form="♀ (female)"]
  R1 = Rotary Potentiometer (Small) [maximum_resistance=100kΩ package=THT]
  R2 = Rotary Potentiometer (Small) [maximum_resistance=100kΩ package=THT]
  S1 = SWITCH-MOMENTARY-2 [package=tactile-pth-12mm]
  S2 = SWITCH-MOMENTARY-2 [package=tactile-pth-12mm]
  S3 = SWITCH-MOMENTARY-2 [package=tactile-pth-12mm]
  S4 = SWITCH-MOMENTARY-2 [package=tactile-pth-12mm]
  S5 = SWITCH-MOMENTARY-2 [package=tactile-pth-12mm]
  S6 = SWITCH-MOMENTARY-2 [package=tactile-pth-12mm]
  S7 = SWITCH-MOMENTARY-2 [package=tactile-pth-12mm]
  S8 = SWITCH-MOMENTARY-2 [package=tactile-pth-12mm]

nets:
  N1: Power_plug1.GND, J1.pin19, R1.leg1, R2.leg1, S2.2, S3.2, S4.2, S5.2, S6.2, S7.2, S8.2
  N2: Power_plug1.VCC, J1.pin20, R1.leg2, R2.leg2
  N3: J1.pin1, R2.wiper
  N4: J1.pin2, R1.wiper
  N5: J1.pin11, S2.1
  N6: J1.pin12, S1.1
  N7: J1.pin13, S4.1
  N8: J1.pin14, S3.1
  N9: J1.pin15, S6.1
  N10: J1.pin16, S5.1
  N11: J1.pin17, S8.1
  N12: J1.pin18, S7.1
