# Fritzing sketch miguel (saved by Fritzing 0.9.2b)
circuit board: 16cm x 10cm

parts:
  R1 = Rotary Potentiometer (Small) [maximum_resistance=100kΩ package=THT]
  R2 = Rotary Potentiometer (Small) [maximum_resistance=100kΩ package=THT]
  R3 = Rotary Potentiometer (Small) [maximum_resistance=100kΩ package=THT]
  R4 = Rotary Potentiometer (Small) [maximum_resistance=100kΩ package=THT]
  J2 = female pin header, 20 pins [form="♀ (female)"]
  Power_plug1 = Power plug
  J1 = double row female pin header, 40 pins [form="♀ (female)"]
  J4 = female pin header, 20 pins [form="♀ (female)"]
  S5 = SWITCH-MOMENTARY-2 [package=tactile-pth-12mm]
  S6 = SWITCH-MOMENTARY-2 [package=tactile-pth-12mm]
  S7 = SWITCH-MOMENTARY-2 [package=tactile-pth-12mm]
  S8 = SWITCH-MOMENTARY-2 [package=tactile-pth-12mm]
  IC1 = SELECTOR_MULTIPLEXER [package=dil16]
  IC2 = SELECTOR_MULTIPLEXER [package=dil16]

nets:
  N1: R1.leg1, R2.leg1, R3.leg1, R4.leg1, J2.pin1, Power_plug1.GND, J1.pin12, J1.pin13, J1.pin14, J1.pin15, J1.pin20, J1.pin29, J4.pin1, S5.1, S5.pin_3, S6.1, S6.pin_3, S7.1, S7.pin_3, S8.1, S8.pin_3, IC1.A_2B, IC1.A_2Y, IC1.P_GND, IC2.A_2B, IC2.A_2Y, IC2.P_GND
  N2: R1.wiper, IC1.A_G
  N3: R1.leg2, R2.leg2, R3.leg2, R4.leg2, J2.pin2, Power_plug1.VCC, J1.pin21, J1.pin26, J1.pin27, J1.pin28, J4.pin2, IC2.P_VCC
  N4: R2.wiper, IC1.A_4A
  N5: R3.wiper, IC1.A_4B
  N6: R4.wiper, IC1.A_4Y
  N7: J2.pin3, J4.pin3, IC1.A_3Y
  N8: J2.pin4, J4.pin4, IC1.A_3B
  N9: J2.pin5, J4.pin5, IC1.A_3A
  N10: J2.pin6, J4.pin6, IC1.A_1B
  N11: J2.pin7, J4.pin7, S8.2, S8.pin_4
  N12: J2.pin8, J4.pin8, S7.2, S7.pin_4
  N13: J2.pin9, J4.pin9, S6.2, S6.pin_4
  N14: J2.pin10, J4.pin10, S5.2, S5.pin_4
  N15: J2.pin11, J4.pin11, IC2.A_3A
  N16: J2.pin12, J4.pin12, IC2.A_3B
  N17: J2.pin13, J4.pin13, IC2.A_3Y
  N18: J2.pin14, J4.pin14, IC2.A_1B
  N19: J2.pin15, J4.pin15
  N20: J2.pin16, J4.pin16
  N21: J2.pin17, J4.pin17
  N22: J2.pin18, J4.pin18
  N23: J2.pin19, J4.pin19
  N24: J2.pin20, J4.pin20
  N25: J1.pin1, J1.pin40, IC2.A_!A!_B
  N26: J1.pin2, J1.pin39, IC2.A_1A
  N27: J1.pin3, J1.pin38, IC2.A_1Y
  N28: J1.pin4, J1.pin37, IC2.A_2A
  N29: J1.pin5, J1.pin36, IC2.A_G
  N30: J1.pin6, J1.pin35, IC2.A_4A
  N31: J1.pin7, J1.pin34, IC2.A_4B
  N32: J1.pin8, J1.pin33, IC2.A_4Y
  N33: J1.pin9, J1.pin32
  N34: J1.pin10, J1.pin31
  N35: J1.pin11, J1.pin30

custom parts:
  SWITCH-MOMENTARY-2: Various NO switches- pushbuttons, reed, etc
