# Fritzing sketch nuno (saved by Fritzing 0.9.2b)
circuit board: 16cm x 10cm
breadboards: 1

parts:
  Power_plug1 = Power plug
  S1 = SWITCH-MOMENTARY-2 [package=tactile-pth-12mm]
  S2 = SWITCH-MOMENTARY-2 [package=tactile-pth-12mm]
  S3 = SWITCH-MOMENTARY-2 [package=tactile-pth-12mm]
  J1 = female pin header, 30 pins [form="♀ (female)"]
  J2 = female pin header, 30 pins [form="♀ (female)"]
  J3 = female pin header, 30 pins [form="♀ (female)"]
  J4 = female pin header, 30 pins [form="♀ (female)"]
  J5 = female pin header, 30 pins [form="♀ (female)"]
  J6 = female pin header, 30 pins [form="♀ (female)"]
  J7 = female pin header, 30 pins [form="♀ (female)"]
  J8 = female pin header, 30 pins [form="♀ (female)"]
  J9 = female pin header, 30 pins [form="♀ (female)"]

nets:
  N1: Power_plug1.GND, S1.1, S1.pin_3, S2.1, S2.pin_3, S3.1, S3.pin_3, J1.pin28, J2.pin28, J3.pin28, J4.pin28, J5.pin28, J6.pin28, J7.pin28, J8.pin28, J9.pin28
  N2: Power_plug1.VCC, J1.pin30, J2.pin30, J3.pin30, J4.pin30, J5.pin30, J6.pin30, J7.pin30, J8.pin30, J9.pin30
  N3: S1.2, S1.pin_4, J8.pin26
  N4: S2.2, S2.pin_4, J8.pin25
  N5: S3.2, S3.pin_4, J8.pin24

custom parts:
  SWITCH-MOMENTARY-2: Various NO switches- pushbuttons, reed, etc
