# Fritzing sketch pedro (saved by Fritzing 0.9.2b)
circuit board: 16cm x 10cm

parts:
  R1 = Rotary Potentiometer (Small) [maximum_resistance=100kΩ package=THT]
  LED1 = LED - 5mm [color="Red (633nm)" package="5 mm [THT]"]
  R2 = Resistor [tolerance=±5% resistance=220 package=THT]
  S1 = SWITCH-MOMENTARY-2 [package=tactile-pth-12mm]
  S2 = SWITCH-MOMENTARY-2 [package=tactile-pth-12mm]
  S3 = SWITCH-MOMENTARY-2 [package=tactile-pth-12mm]
  Power_plug1 = Power plug
  J1 = female pin header, 10 pins [form="♀ (female)"]

nets:
  N1: R1.leg1, Power_plug1.VCC, J1.pin1
  N2: R1.wiper, J1.pin3
  N3: R1.leg2, R2.Pin_0, S1.2, S1.pin_4, S2.2, S3.1, S3.pin_3, Power_plug1.GND, J1.pin2
  N4: LED1.cathode, R2.Pin_1
  N5: LED1.anode, J1.pin4
  N6: S1.1, S1.pin_3, J1.pin5
  N7: S2.1, S2.pin_3, J1.pin6
  N8: S3.2, S3.pin_4, J1.pin7

custom parts:
  SWITCH-MOMENTARY-2: Various NO switches- pushbuttons, reed, etc
