# Fritzing sketch rafael (saved by Fritzing 0.9.2b)
circuit board: 16cm x 10cm

parts:
  LED1 = LED - 5mm [color="Red (633nm)" package="5 mm [THT]"]
  LED2 = LED - 5mm [color="Red (633nm)" package="5 mm [THT]"]
  LED3 = LED - 5mm [color="Red (633nm)" package="5 mm [THT]"]
  LED4 = LED - 5mm [color="Red (633nm)" package="5 mm [THT]"]
  LED5 = LED - 5mm [color="Red (633nm)" package="5 mm [THT]"]
  LED6 = LED - 5mm [color="Red (633nm)" package="5 mm [THT]"]
  LED7 = LED - 5mm [color="Red (633nm)" package="5 mm [THT]"]
  LED8 = LED - 5mm [color="Red (633nm)" package="5 mm [THT]"]
  LED9 = LED - 5mm [color="Red (633nm)" package="5 mm [THT]"]
  LED10 = LED - 5mm [color="Red (633nm)" package="5 mm [THT]"]
  LED11 = LED - 5mm [color="Red (633nm)" package="5 mm [THT]"]
  LED12 = LED - 5mm [color="Red (633nm)" package="5 mm [THT]"]
  R1 = Resistor [tolerance=±5% resistance=220 package=THT]
  R2 = Resistor [tolerance=±5% resistance=220 package=THT]
  R3 = Resistor [tolerance=±5% resistance=220 package=THT]
  R4 = Resistor [tolerance=±5% resistance=220 package=THT]
  R5 = Resistor [tolerance=±5% resistance=220 package=THT]
  R6 = Resistor [tolerance=±5% resistance=220 package=THT]
  R7 = Resistor [tolerance=±5% resistance=220 package=THT]
  R8 = Resistor [tolerance=±5% resistance=220 package=THT]
  R9 = Resistor [tolerance=±5% resistance=220 package=THT]
  R10 = Resistor [tolerance=±5% resistance=220 package=THT]
  R11 = Resistor [tolerance=±5% resistance=220 package=THT]
  R12 = Resistor [tolerance=±5% resistance=220 package=THT]
  R13 = Rotary Potentiometer (Small) [maximum_resistance=100kΩ package=THT]
  R16 = Rotary Potentiometer (Small) [maximum_resistance=100kΩ package=THT]
  Power_plug1 = Power plug
  S6 = SWITCH-MOMENTARY-2 [package=tactile-pth-12mm]
  S7 = SWITCH-MOMENTARY-2 [package=tactile-pth-12mm]
  S8 = SWITCH-MOMENTARY-2 [package=tactile-pth-12mm]
  S10 = SWITCH-MOMENTARY-2 [package=tactile-pth-12mm]
  S11 = SWITCH-MOMENTARY-2 [package=tactile-pth-12mm]
  IC2 = SELECTOR_MULTIPLEXER [package=dil16]
  J1 = female alternating pin header, 20 pins [form="♀ (female)"]
  J2 = female pin header, 10 pins [form="♀ (female)"]
  IC3 = SELECTOR_MULTIPLEXER [package=dil16]

nets:
  N1: LED1.cathode, R12.Pin_0
  N2: LED1.anode, IC2.A_!A!_B
  N3: LED2.cathode, R11.Pin_0
  N4: LED2.anode, IC3.A_!A!_B
  N5: LED3.cathode, R10.Pin_1
  N6: LED3.anode, IC3.A_1Y
  N7: LED4.cathode, R9.Pin_1
  N8: LED4.anode, IC3.A_2A
  N9: LED5.cathode, R8.Pin_1
  N10: LED5.anode, IC3.A_1A
  N11: LED6.cathode, R7.Pin_1
  N12: LED6.anode, IC2.A_G
  N13: LED7.cathode, R6.Pin_1
  N14: LED7.anode, IC2.A_4A
  N15: LED8.cathode, R5.Pin_1
  N16: LED8.anode, IC2.A_4B
  N17: LED9.cathode, R4.Pin_0
  N18: LED9.anode, IC2.A_4Y
  N19: LED10.cathode, R3.Pin_0
  N20: LED10.anode, IC2.A_1A
  N21: LED11.cathode, R2.Pin_0
  N22: LED11.anode, IC2.A_1Y
  N23: LED12.cathode, R1.Pin_0
  N24: LED12.anode, IC2.A_2A
  N25: R1.Pin_1, R2.Pin_1, R3.Pin_1, R4.Pin_1, R5.Pin_0, R6.Pin_0, R7.Pin_0, R8.Pin_0, R9.Pin_0, R10.Pin_0, R11.Pin_1, R12.Pin_1, R13.leg1, R16.leg1, Power_plug1.GND, S6.1, S6.pin_3, S7.2, S7.pin_4, S8.2, S8.pin_4, S10.2, S10.pin_4, S11.2, S11.pin_4, IC2.A_2B, IC2.A_2Y, IC2.P_GND, J1.pin2, J1.pin12, IC3.A_2B, IC3.A_2Y, IC3.P_GND
  N26: R13.leg2, R16.leg2, Power_plug1.VCC, IC2.P_VCC, J1.pin1, IC3.P_VCC
  N27: R16.wiper, J1.pin11
  N28: S7.1, S7.pin_3, J1.pin14
  N29: S8.1, S8.pin_3, J1.pin16
  N30: S10.1, S10.pin_3, J1.pin15
  N31: S11.1, S11.pin_3, J1.pin13
  N32: IC2.A_1B, J2.pin7
  N33: IC2.A_3Y, J2.pin10
  N34: IC2.A_3B, J2.pin9
  N35: IC2.A_3A, J2.pin8
  N36: J1.pin17, IC3.A_3Y
  N37: J1.pin18, IC3.A_3B
  N38: J1.pin19, IC3.A_3A
  N39: J1.pin20, IC3.A_1B

custom parts:
  SWITCH-MOMENTARY-2: Various NO switches- pushbuttons, reed, etc
