# Fritzing sketch rolando (saved by Fritzing 0.9.2b)
circuit board: 16cm x 10cm

parts:
  S1 = SWITCH-MOMENTARY-2 [package=tactile-pth-12mm]
  S2 = SWITCH-MOMENTARY-2 [package=tactile-pth-12mm]
  S3 = SWITCH-MOMENTARY-2 [package=tactile-pth-12mm]
  S4 = SWITCH-MOMENTARY-2 [package=tactile-pth-12mm]
  S5 = SWITCH-MOMENTARY-2 [package=tactile-pth-12mm]
  S6 = SWITCH-MOMENTARY-2 [package=tactile-pth-12mm]
  S7 = SWITCH-MOMENTARY-2 [package=tactile-pth-12mm]
  S8 = SWITCH-MOMENTARY-2 [package=tactile-pth-12mm]
  S9 = SWITCH-MOMENTARY-2 [package=tactile-pth-12mm]
  S10 = SWITCH-MOMENTARY-2 [package=tactile-pth-12mm]
  S11 = SWITCH-MOMENTARY-2 [package=tactile-pth-12mm]
  S12 = SWITCH-MOMENTARY-2 [package=tactile-pth-12mm]
  S13 = SWITCH-MOMENTARY-2 [package=tactile-pth-12mm]
  S14 = SWITCH-MOMENTARY-2 [package=tactile-pth-12mm]
  S15 = SWITCH-MOMENTARY-2 [package=tactile-pth-12mm]
  S16 = SWITCH-MOMENTARY-2 [package=tactile-pth-12mm]
  S17 = SWITCH-MOMENTARY-2 [package=tactile-pth-12mm]
  S18 = SWITCH-MOMENTARY-2 [package=tactile-pth-12mm]
  S19 = SWITCH-MOMENTARY-2 [package=tactile-pth-12mm]
  S20 = SWITCH-MOMENTARY-2 [package=tactile-pth-12mm]
  S21 = SWITCH-MOMENTARY-2 [package=tactile-pth-12mm]
  S22 = SWITCH-MOMENTARY-2 [package=tactile-pth-12mm]
  S23 = SWITCH-MOMENTARY-2 [package=tactile-pth-12mm]
  S24 = SWITCH-MOMENTARY-2 [package=tactile-pth-12mm]
  S25 = SWITCH-MOMENTARY-2 [package=tactile-pth-12mm]
  S26 = SWITCH-MOMENTARY-2 [package=tactile-pth-12mm]
  S27 = SWITCH-MOMENTARY-2 [package=tactile-pth-12mm]
  S28 = SWITCH-MOMENTARY-2 [package=tactile-pth-12mm]
  S29 = SWITCH-MOMENTARY-2 [package=tactile-pth-12mm]
  S30 = SWITCH-MOMENTARY-2 [package=tactile-pth-12mm]
  S31 = SWITCH-MOMENTARY-2 [package=tactile-pth-12mm]
  S32 = SWITCH-MOMENTARY-2 [package=tactile-pth-12mm]
  S33 = SWITCH-MOMENTARY-2 [package=tactile-pth-12mm]
  S34 = SWITCH-MOMENTARY-2 [package=tactile-pth-12mm]
  S35 = SWITCH-MOMENTARY-2 [package=tactile-pth-12mm]
  S36 = SWITCH-MOMENTARY-2 [package=tactile-pth-12mm]
  IC1 = SELECTOR_MULTIPLEXER [package=dil16]
  Power_plug1 = Power plug
  IC2 = SELECTOR_MULTIPLEXER [package=dil16]
  IC3 = SELECTOR_MULTIPLEXER [package=dil16]
  IC4 = SELECTOR_MULTIPLEXER [package=dil16]
  IC5 = SELECTOR_MULTIPLEXER [package=dil16]
  J1 = female pin header, 6 pins [form="♀ (female)"]
  J2 = female pin header, 6 pins [form="♀ (female)"]
  J3 = female pin header, 6 pins [form="♀ (female)"]
  J4 = female pin header, 6 pins [form="♀ (female)"]
  J5 = female pin header, 6 pins [form="♀ (female)"]
  J6 = female pin header, 6 pins [form="♀ (female)"]
  J7 = female pin header, 6 pins [form="♀ (female)"]
  J8 = female pin header, 6 pins [form="♀ (female)"]
  J9 = female pin header, 6 pins [form="♀ (female)"]
  J10 = female pin header, 6 pins [form="♀ (female)"]
  J11 = female pin header, 6 pins [form="♀ (female)"]
  J12 = female pin header, 6 pins [form="♀ (female)"]
  J13 = female pin header, 6 pins [form="♀ (female)"]
  J14 = female pin header, 6 pins [form="♀ (female)"]
  J15 = female pin header, 6 pins [form="♀ (female)"]
  J16 = female pin header, 6 pins [form="♀ (female)"]
  J17 = female pin header, 6 pins [form="♀ (female)"]
  J18 = female pin header, 6 pins [form="♀ (female)"]
  J19 = female pin header, 6 pins [form="♀ (female)"]
  J20 = female pin header, 6 pins [form="♀ (female)"]

nets:
  N1: S1.1, S1.pin_3, S2.1, S2.pin_3, S3.1, S3.pin_3, S4.1, S4.pin_3, S5.1, S5.pin_3, S6.1, S6.pin_3, S7.1, S7.pin_3, S8.1, S8.pin_3, S9.1, S9.pin_3, S10.1, S10.pin_3, S11.1, S11.pin_3, S12.1, S12.pin_3, S13.1, S13.pin_3, S14.1, S14.pin_3, S15.1, S15.pin_3, S16.1, S16.pin_3, S17.1, S17.pin_3, S18.1, S18.pin_3, S19.1, S19.pin_3, S20.1, S20.pin_3, S21.1, S21.pin_3, S22.1, S22.pin_3, S23.1, S23.pin_3, S24.1, S24.pin_3, S25.1, S25.pin_3, S26.1, S26.pin_3, S27.1, S27.pin_3, S28.1, S28.pin_3, S29.1, S29.pin_3, S30.1, S30.pin_3, S31.1, S31.pin_3, S32.1, S32.pin_3, S33.1, S33.pin_3, S34.pin_3, S35.1, S35.pin_3, S36.1, S36.pin_3, IC1.A_2B, IC1.A_2Y, IC1.P_GND, Power_plug1.GND, IC2.A_2B, IC2.A_2Y, IC2.P_GND, IC3.A_2B, IC3.A_2Y, IC3.P_GND, IC4.A_2B, IC4.A_2Y, IC4.P_GND, IC5.A_2B, IC5.A_2Y, IC5.P_GND, J1.pin6, J2.pin6, J3.pin6, J4.pin6, J5.pin6, J6.pin6, J7.pin6, J8.pin6, J9.pin6, J10.pin6, J11.pin6, J12.pin6, J13.pin6, J14.pin6, J15.pin6, J16.pin6, J17.pin6, J18.pin6, J19.pin6, J20.pin6
  N2: S1.2, S1.pin_4, IC1.A_2A
  N3: S2.2, S2.pin_4, IC1.A_!A!_B
  N4: S3.2, S3.pin_4, IC2.A_1Y
  N5: S4.2, IC1.A_4B
  N6: S5.2, S5.pin_4, IC3.A_4A
  N7: S6.2, S6.pin_4, IC2.A_4Y
  N8: S7.2, S7.pin_4, IC3.A_1A
  N9: S8.2, IC2.A_G
  N10: S9.2, S9.pin_4, IC4.A_!A!_B
  N11: S10.2, S10.pin_4, IC4.A_4B
  N12: S11.2, S11.pin_4, IC4.A_2A
  N13: S12.2, S12.pin_4, IC5.A_1Y
  N14: S13.2, S13.pin_4, IC4.A_G
  N15: S14.2, IC1.A_4Y
  N16: S15.2, S15.pin_4, IC3.A_4B
  N17: S16.2, S16.pin_4, IC1.A_G
  N18: S17.2, S17.pin_4, IC5.A_G
  N19: S18.2, IC3.A_!A!_B
  N20: S19.2, S19.pin_4, IC4.A_4Y
  N21: S20.2, S20.pin_4, IC1.A_1Y
  N22: S21.2, S21.pin_4, IC3.A_2A
  N23: S22.2, S22.pin_4, IC2.A_1A
  N24: S23.2, IC2.A_4A
  N25: S24.2, S24.pin_4, IC4.A_1Y
  N26: S25.2, S25.pin_4, IC1.A_1A
  N27: S26.2, IC2.A_4B
  N28: S27.2, S27.pin_4, IC3.A_4Y
  N29: S28.2, S28.pin_4, IC3.A_1Y
  N30: S29.2, S29.pin_4, IC1.A_4A
  N31: S30.2, IC3.A_G
  N32: S31.2, IC2.A_2A
  N33: S32.2, S32.pin_4, IC4.A_1A
  N34: S33.2, S33.pin_4, IC5.A_4A
  N35: S34.2, S34.pin_4, IC4.A_4A
  N36: S35.2, S35.pin_4, IC5.A_2A
  N37: S36.2, S36.pin_4, IC2.A_!A!_B
  N38: IC1.A_1B, J1.pin5, J2.pin5, J3.pin5, J4.pin5
  N39: IC1.A_3Y, J1.pin3, J2.pin3, J3.pin3, J4.pin3
  N40: IC1.A_3B, J1.pin2, J2.pin2, J3.pin2, J4.pin2
  N41: IC1.A_3A, J1.pin1, J2.pin1, J3.pin1, J4.pin1
  N42: IC1.P_VCC, Power_plug1.VCC, IC2.P_VCC, IC3.P_VCC, IC4.P_VCC, IC5.P_VCC, J1.pin4, J2.pin4, J3.pin4, J4.pin4, J5.pin4, J6.pin4, J7.pin4, J8.pin4, J9.pin4, J10.pin4, J11.pin4, J12.pin4, J13.pin4, J14.pin4, J15.pin4, J16.pin4, J17.pin4, J18.pin4, J19.pin4, J20.pin4
  N43: IC2.A_1B, J5.pin5, J6.pin5, J7.pin5, J8.pin5
  N44: IC2.A_3Y, J5.pin3, J6.pin3, J7.pin3, J8.pin3
  N45: IC2.A_3B, J5.pin2, J6.pin2, J7.pin2, J8.pin2
  N46: IC2.A_3A, J5.pin1, J6.pin1, J7.pin1, J8.pin1
  N47: IC3.A_1B, J9.pin5, J10.pin5, J11.pin5, J12.pin5
  N48: IC3.A_3Y, J9.pin3, J10.pin3, J11.pin3, J12.pin3
  N49: IC3.A_3B, J9.pin2, J10.pin2, J11.pin2, J12.pin2
  N50: IC3.A_3A, J9.pin1, J10.pin1, J11.pin1, J12.pin1
  N51: IC4.A_1B, J13.pin5, J14.pin5, J15.pin5, J16.pin5
  N52: IC4.A_3Y, J13.pin3, J14.pin3, J15.pin3, J16.pin3
  N53: IC4.A_3B, J13.pin2, J14.pin2, J15.pin2, J16.pin2
  N54: IC4.A_3A, J13.pin1, J14.pin1, J15.pin1, J16.pin1
  N55: IC5.A_1B, J17.pin5, J18.pin5, J19.pin5, J20.pin5
  N56: IC5.A_3Y, J17.pin3, J18.pin3, J19.pin3, J20.pin3
  N57: IC5.A_3B, J17.pin2, J18.pin2, J19.pin2, J20.pin2
  N58: IC5.A_3A, J17.pin1, J18.pin1, J19.pin1, J20.pin1

custom parts:
  SWITCH-MOMENTARY-2: Various NO switches- pushbuttons, reed, etc
